# Fritzing sketch CTD logger (saved by Fritzing 1.0.0rc)
breadboards: 1

parts:
  Logger = OpenLog
  MAX3232 = IC, SIP package, 10 pins [chip_label=Transceiver]
  CTD = IC, SIP package, 3 pins [chip_label=CTD]
  J1 = screw terminal, 4 pins
  LCB = IC, SIP package, 8 pins [chip_label=LCB]

nets:
  N1: Logger.RXI, MAX3232.pin9
  N2: Logger.TXO, MAX3232.pin7
  5V: Logger.VCC, MAX3232.pin5, J1.pin1
  GND: Logger.GND, MAX3232.pin6, CTD.pin3, J1.pin4
  N3: MAX3232.pin1, J1.pin3, LCB.pin4
  N4: MAX3232.pin3, CTD.pin2, J1.pin2
  N5: CTD.pin1, LCB.pin3

notes:
  red - power, 5V (min 3.3V)
  blue - data from CTD (16 Hz)
  orange - data to lander control board (1 Hz)
  green - data from lander control board to CTD
  black - ground
  from CTD
  return to CTD
  R1IN (RS-232) → R1OUT (TTL)
  T1IN (TTL) → T1OUT (RS-232)
